# Fritzing sketch Oving4 (saved by Fritzing 0.9.3b)
breadboards: 1

parts:
  HC-SR04_Sensor_1 = HC-SR04 Ultrasonic Distance Sensor
  Part1 = Arduino Uno (Rev3)
  J1 = Basic Servo
  Part2 = Bluetooth HC-05 Macho

nets:
  VCC: HC-SR04_Sensor_1.VCC, Part1.5V, J1.vcc, Part2.VCC
  N1: HC-SR04_Sensor_1.TRIG, Part1.A1
  N2: HC-SR04_Sensor_1.ECHO, Part1.A0
  GND: HC-SR04_Sensor_1.GND, Part1.GND, J1.gnd, Part2.GND
  N3: Part1.D1/TX, Part2.RXD
  N4: Part1.D2, Part2.TXD
